// Logisim project cpu.circ as structural Verilog: 14 circuits, main circuit main
module main (
  input  reset
);

  wire alu_1_eqz, alu_1_neg, ALUimm, and_1_out, and_2_out, beqz, blt, BR, clk, controlled_buffer_1_out, DMwe,
       keyboard_1_avail, keyboardIn, memory_latch_1_oe_latched, memory_latch_1_we_latched, nclk, NoData,
       or_1_out, Rdst, Rwd, Rwe, TTYoutput, writeToMem;
  wire [1:0] jump;
  wire [2:0] ALUopp, multiplexer_2_out, multiplexer_4_out;
  wire [3:0] opcode;
  wire [5:0] immediate;
  wire [6:0] ASCIIData, TTYInData;
  wire [11:0] address, JumpDestination;
  wire [15:0] adder16bit_2_out1, alu_1_outputd, bit_extender_1_out, BranchDistance,
       memory_latch_1_address_latched, memory_latch_1_data_in_latched, multiplexer_1_out, multiplexer_3_out,
       multiplexer_5_out, multiplexer_7_out, multiplexer_8_out, multiplexer_9_out, PCValue, ram_1_dout,
       RegisterDestination, registerfile_1_reg2contents, rom_1_data, singleregister_1_dataout;

  Clock u_clk (.out(clk));
  not not_1 (nclk, clk);
  ROM #(.addrWidth(16), .dataWidth(16)) rom_1 (.addr(singleregister_1_dataout), .data(rom_1_data));
  SingleRegister singleregister_1 (
    .dataIn(multiplexer_8_out), .reset(reset), .clk(nclk), .writeEnable(1'b1),
    .dataOut(singleregister_1_dataout));
  control control_1 (
    .opcode(opcode), .in1(keyboardIn), .ou1(TTYoutput), .writeToMem(writeToMem), .Rwe(Rwe), .Rdst(Rdst),
    .ALUimm(ALUimm), .DMwe(DMwe), .Rwd(Rwd), .BR(BR), .blt(blt), .beqz(beqz), .jump0(jump[0]), .jump1(jump[1]));
  adder16Bit adder16bit_1 (
    .in_1(1'b0), .input2(16'h1), .input1(singleregister_1_dataout), .out1(PCValue));  // open: ovf
  decode decode_1 (
    .input1(rom_1_data), .address(address), .imm(immediate), .Shamt(JumpDestination[2:0]),
    .Rd(JumpDestination[5:3]), .Rt(JumpDestination[8:6]), .Rs(JumpDestination[11:9]), .Opcode(opcode));
  adder16Bit adder16bit_2 (.input2(BranchDistance), .input1(PCValue), .out1(adder16bit_2_out1));  // open: in_1, ovf
  Multiplexer #(.width(16), .enable("false")) multiplexer_1 (
    .in0(PCValue), .in1(adder16bit_2_out1), .out(multiplexer_1_out), .sel(or_1_out));
  Multiplexer #(.width(3), .enable("false")) multiplexer_2 (
    .in0(JumpDestination[8:6]), .in1(JumpDestination[5:3]), .out(multiplexer_2_out), .sel(Rdst));
  or or_1 (or_1_out, and_1_out, and_2_out);
  Multiplexer #(.width(16), .enable("false")) multiplexer_3 (
    .in0(multiplexer_5_out), .in1({{8{1'b0}}, NoData, ASCIIData}), .out(multiplexer_3_out), .sel(keyboardIn));
  Multiplexer #(.select(2), .width(3), .enable("false")) multiplexer_4 (
    .in0(multiplexer_2_out), .in3(3'b111), .out(multiplexer_4_out), .sel(jump));  // open: in1, in2
  Keyboard #(.trigger("falling")) keyboard_1 (
    .clk(controlled_buffer_1_out), .clr(reset), .avail(keyboard_1_avail), .data(ASCIIData));  // open: re
  assign controlled_buffer_1_out = keyboardIn ? nclk : 1'bz;  // Controlled_Buffer controlled_buffer_1
  and and_1 (and_1_out, blt, alu_1_neg);
  and and_2 (and_2_out, beqz, alu_1_eqz);
  Multiplexer #(.select(2), .width(16), .enable("false")) multiplexer_5 (
    .in0(multiplexer_9_out), .in3(PCValue), .out(multiplexer_5_out), .sel(jump));  // open: in1, in2
  not not_2 (NoData, keyboard_1_avail);
  Multiplexer #(.width(7), .enable("false")) multiplexer_6 (
    .in0(RegisterDestination[6:0]), .in1({7{1'b0}}), .out(TTYInData), .sel(TTYoutput));
  RegisterFile registerfile_1 (
    .clk(clk), .reset(reset), .WriteData(multiplexer_3_out), .RegWriteEnable(Rwe),
    .WritePort(multiplexer_4_out), .ReadReg1(JumpDestination[11:9]), .ReadReg2(JumpDestination[8:6]),
    .Reg1Contents(RegisterDestination), .Reg2Contents(registerfile_1_reg2contents));
  Multiplexer #(.width(16), .enable("false")) multiplexer_7 (
    .in0(registerfile_1_reg2contents), .in1(bit_extender_1_out), .out(multiplexer_7_out), .sel(ALUimm));
  assign bit_extender_1_out = {{10{immediate[5]}}, immediate};  // Bit_Extender bit_extender_1
  Multiplexer #(.select(2), .width(16), .enable("false")) multiplexer_8 (
    .in0(multiplexer_1_out), .in1({4'b0000, JumpDestination}), .in2(RegisterDestination),
    .in3({4'b0000, JumpDestination}), .out(multiplexer_8_out), .sel(jump));
  TTY #(.rows(13), .cols(80)) tty_1 (.data(TTYInData), .clk(clk), .we(reset));  // open: clr
  ALU alu_1 (
    .shiftValue(JumpDestination[2:0]), .InputData1(RegisterDestination), .InputData2(multiplexer_7_out),
    .OpType(ALUopp), .OutputD(alu_1_outputd), .eqz(alu_1_eqz), .neg(alu_1_neg));
  memory_latch memory_latch_1 (
    .address(alu_1_outputd), .WE(DMwe), .clk(nclk), .data_in(registerfile_1_reg2contents),
    .address_latched(memory_latch_1_address_latched), .WE_latched(memory_latch_1_we_latched),
    .OE_latched(memory_latch_1_oe_latched), .data_in_latched(memory_latch_1_data_in_latched));
  RAM #(.addrWidth(16), .dataWidth(16), .trigger("high"), .databus("bibus")) ram_1 (
    .addr(memory_latch_1_address_latched), .we(memory_latch_1_we_latched), .oe(memory_latch_1_oe_latched),
    .din(memory_latch_1_data_in_latched), .dout(ram_1_dout));
  Multiplexer #(.width(16), .enable("false")) multiplexer_9 (
    .in0(alu_1_outputd), .in1(ram_1_dout), .out(multiplexer_9_out), .sel(writeToMem));

  // Other names for the same wires on the sheet: shamt[2:0] = JumpDestination[2:0]; rd[2:0] = JumpDestination[5:3];
  //   rt[2:0] = JumpDestination[8:6]; rs[2:0] = JumpDestination[11:9]
endmodule

module memory_latch (
  input  [15:0] address,
  input  WE,
  input  clk,
  input  [15:0] data_in,
  output [15:0] address_latched,
  output WE_latched,
  output OE_latched,
  output [15:0] data_in_latched
);

  wire DMwe_latch_q;
  wire [15:0] addr_latch_q;

  Register #(.width(16), .trigger("falling")) addr_latch (
    .D(address), .en(WE), .clk(clk), .Q(addr_latch_q));  // open: clr
  D_Flip_Flop #(.trigger("falling")) DMwe_latch (.D(WE), .clk(clk), .Q(DMwe_latch_q));  // open: Qn, preset, reset
  Register #(.width(16), .trigger("falling")) data_to_be_written (
    .D(data_in), .en(WE), .clk(clk), .Q(data_in_latched));  // open: clr
  Multiplexer #(.width(16), .enable("false")) multiplexer_1 (
    .in0(address), .in1(addr_latch_q), .out(address_latched), .sel(DMwe_latch_q));
  and and_1 (WE_latched, clk, DMwe_latch_q);
  not not_1 (OE_latched, WE_latched);
endmodule

module logRAM (
);

  wire DMwe, memory_latch_1_oe_latched, memory_latch_1_we_latched, nclk;
  wire [15:0] memory_latch_1_address_latched, memory_latch_1_data_in_latched;

  memory_latch memory_latch_1 (
    .WE(DMwe), .clk(nclk), .address_latched(memory_latch_1_address_latched),
    .WE_latched(memory_latch_1_we_latched), .OE_latched(memory_latch_1_oe_latched),
    .data_in_latched(memory_latch_1_data_in_latched));  // open: address, data_in
  RAM #(.addrWidth(16), .dataWidth(16), .trigger("high"), .databus("bibus")) ram_1 (
    .addr(memory_latch_1_address_latched), .we(memory_latch_1_we_latched), .oe(memory_latch_1_oe_latched),
    .din(memory_latch_1_data_in_latched));  // open: dout
endmodule

module ALU (
  input  [2:0] shiftValue,
  input  [15:0] InputData1,
  input  [15:0] InputData2,
  input  [2:0] OpType,
  output [15:0] OutputD,
  output eqz,
  output neg
);

  wire [15:0] adder16bit_1_out1, adder16bit_2_out1, leftshifter_1_output1, not_1_out, rightshifter_1_output1,
       xor_1_out;

  leftShifter leftshifter_1 (.input1(InputData1), .shamt(shiftValue), .output1(leftshifter_1_output1));
  rightShifter rightshifter_1 (.input1(InputData1), .shamt(shiftValue), .output1(rightshifter_1_output1));
  adder16Bit adder16bit_1 (.input2(InputData1), .input1(InputData2), .out1(adder16bit_1_out1));  // open: in_1, ovf
  adder16Bit adder16bit_2 (.input2(InputData2), .input1(InputData1), .out1(adder16bit_2_out1));  // open: in_1, ovf
  assign not_1_out = ~InputData1;  // NOT_Gate not_1, 16 bits wide
  assign xor_1_out = InputData1 ^ InputData2;  // XOR_Gate xor_1, 16 bits wide
  Multiplexer #(.select(3), .width(16), .enable("false")) multiplexer_1 (
    .in0(leftshifter_1_output1), .in1(rightshifter_1_output1), .in2(adder16bit_1_out1),
    .in3(adder16bit_2_out1), .in4(xor_1_out), .in5(not_1_out), .out(OutputD), .sel(OpType));  // open: in6, in7
  compare compare_1 (.in_1(OutputD), .equalToZero(eqz), .neg(neg));
endmodule

module RegisterFile (
  input  clk,
  input  reset,
  input  [15:0] WriteData,
  input  RegWriteEnable,
  input  [2:0] WritePort,
  input  [2:0] ReadReg1,
  input  [2:0] ReadReg2,
  output [15:0] Reg1Contents,
  output [15:0] Reg2Contents
);

  wire out1bit0, out1bit1, out1bit2, out1bit3, out1bit4, out1bit5, out1bit6, out1bit7, out2bit0, out2bit1,
       out2bit2, out2bit3, out2bit4, out2bit5, out2bit6, out2bit7, WE0, WE1, WE2, WE3, WE4, WE5, WE6, WE7;
  wire [15:0] and_1_out, Q0, Q1, Q2, Q3, Q4, Q5, Q6, Q7;

  assign and_1_out = WriteData & {16{1'b0}};  // AND_Gate and_1, 16 bits wide
  Decoder #(.select(3)) decoder_1 (
    .out0(WE0), .out1(WE1), .out2(WE2), .out3(WE3), .out4(WE4), .out5(WE5), .out6(WE6), .out7(WE7),
    .sel(WritePort), .en(RegWriteEnable));
  Decoder #(.select(3)) decoder_2 (
    .out0(out1bit0), .out1(out1bit1), .out2(out1bit2), .out3(out1bit3), .out4(out1bit4), .out5(out1bit5),
    .out6(out1bit6), .out7(out1bit7), .sel(ReadReg1));  // open: en
  // Probe on Q0
  SingleRegister reg0 (.dataIn(and_1_out), .reset(reset), .clk(clk), .writeEnable(WE0), .dataOut(Q0));
  // Probe on Q1
  SingleRegister singleregister_1 (.dataIn(WriteData), .reset(reset), .clk(clk), .writeEnable(WE1), .dataOut(Q1));
  // Probe on Q2
  SingleRegister singleregister_2 (.dataIn(WriteData), .reset(reset), .clk(clk), .writeEnable(WE2), .dataOut(Q2));
  // Probe on Q3
  SingleRegister singleregister_3 (.dataIn(WriteData), .reset(reset), .clk(clk), .writeEnable(WE3), .dataOut(Q3));
  Decoder #(.select(3)) decoder_3 (
    .out0(out2bit0), .out1(out2bit1), .out2(out2bit2), .out3(out2bit3), .out4(out2bit4), .out5(out2bit5),
    .out6(out2bit6), .out7(out2bit7), .sel(ReadReg2));  // open: en
  SingleRegister singleregister_4 (.dataIn(WriteData), .reset(reset), .clk(clk), .writeEnable(WE1), .dataOut(Q4));
  // Probe on Q4
  // Probe on Q5
  SingleRegister singleregister_5 (.dataIn(WriteData), .reset(reset), .clk(clk), .writeEnable(WE1), .dataOut(Q5));
  // Probe on Q6
  SingleRegister singleregister_6 (.dataIn(WriteData), .reset(reset), .clk(clk), .writeEnable(WE1), .dataOut(Q6));
  // Probe on Q7
  SingleRegister singleregister_7 (.dataIn(WriteData), .reset(reset), .clk(clk), .writeEnable(WE1), .dataOut(Q7));
  assign Reg1Contents = out1bit0 ? Q0 : 16'bz;  // Controlled_Buffer controlled_buffer_1
  assign Reg1Contents = out1bit1 ? Q1 : 16'bz;  // Controlled_Buffer controlled_buffer_2
  assign Reg1Contents = out1bit2 ? Q2 : 16'bz;  // Controlled_Buffer controlled_buffer_3
  assign Reg1Contents = out1bit3 ? Q3 : 16'bz;  // Controlled_Buffer controlled_buffer_4
  assign Reg1Contents = out1bit4 ? Q4 : 16'bz;  // Controlled_Buffer controlled_buffer_5
  assign Reg1Contents = out1bit5 ? Q5 : 16'bz;  // Controlled_Buffer controlled_buffer_6
  assign Reg1Contents = out1bit6 ? Q6 : 16'bz;  // Controlled_Buffer controlled_buffer_7
  assign Reg1Contents = out1bit7 ? Q7 : 16'bz;  // Controlled_Buffer controlled_buffer_8
  assign Reg2Contents = out2bit0 ? Q0 : 16'bz;  // Controlled_Buffer controlled_buffer_9
  assign Reg2Contents = out2bit1 ? Q1 : 16'bz;  // Controlled_Buffer controlled_buffer_10
  assign Reg2Contents = out2bit2 ? Q2 : 16'bz;  // Controlled_Buffer controlled_buffer_11
  assign Reg2Contents = out2bit3 ? Q3 : 16'bz;  // Controlled_Buffer controlled_buffer_12
  assign Reg2Contents = out2bit4 ? Q4 : 16'bz;  // Controlled_Buffer controlled_buffer_13
  assign Reg2Contents = out2bit5 ? Q5 : 16'bz;  // Controlled_Buffer controlled_buffer_14
  assign Reg2Contents = out2bit6 ? Q6 : 16'bz;  // Controlled_Buffer controlled_buffer_15
  assign Reg2Contents = out2bit7 ? Q7 : 16'bz;  // Controlled_Buffer controlled_buffer_16
endmodule

module SingleRegister (
  input  [15:0] dataIn,
  input  reset,
  input  clk,
  input  writeEnable,
  output [15:0] dataOut
);

  wire clk_t;

  and and_1 (clk_t, clk, writeEnable);
  D_Flip_Flop d_ff_1 (.D(dataIn[0]), .clk(clk_t), .Q(dataOut[0]));  // open: Qn, preset, reset
  D_Flip_Flop d_ff_2 (.D(dataIn[4]), .clk(clk_t), .Q(dataOut[4]), .reset(reset));  // open: Qn, preset
  D_Flip_Flop d_ff_3 (.D(dataIn[8]), .clk(clk_t), .Q(dataOut[8]), .reset(reset));  // open: Qn, preset
  D_Flip_Flop d_ff_4 (.D(dataIn[12]), .clk(clk_t), .Q(dataOut[12]), .reset(reset));  // open: Qn, preset
  D_Flip_Flop d_ff_5 (.D(dataIn[1]), .clk(clk_t), .Q(dataOut[1]), .reset(clk_t));  // open: Qn, preset
  D_Flip_Flop d_ff_6 (.D(dataIn[5]), .clk(clk_t), .Q(dataOut[5]), .reset(clk_t));  // open: Qn, preset
  D_Flip_Flop d_ff_7 (.D(dataIn[9]), .clk(clk_t), .Q(dataOut[9]), .reset(clk_t));  // open: Qn, preset
  D_Flip_Flop d_ff_8 (.D(dataIn[13]), .clk(clk_t), .Q(dataOut[13]), .reset(clk_t));  // open: Qn, preset
  D_Flip_Flop d_ff_9 (.D(dataIn[2]), .clk(clk_t), .Q(dataOut[2]), .reset(reset));  // open: Qn, preset
  D_Flip_Flop d_ff_10 (.D(dataIn[6]), .clk(clk_t), .Q(dataOut[6]), .reset(reset));  // open: Qn, preset
  D_Flip_Flop d_ff_11 (.D(dataIn[10]), .clk(clk_t), .Q(dataOut[10]), .reset(reset));  // open: Qn, preset
  D_Flip_Flop d_ff_12 (.D(dataIn[14]), .clk(clk_t), .Q(dataOut[14]), .reset(reset));  // open: Qn, preset
  D_Flip_Flop d_ff_13 (.D(dataIn[3]), .clk(clk_t), .Q(dataOut[3]), .reset(reset));  // open: Qn, preset
  D_Flip_Flop d_ff_14 (.D(dataIn[7]), .clk(clk_t), .Q(dataOut[7]), .reset(reset));  // open: Qn, preset
  D_Flip_Flop d_ff_15 (.D(dataIn[11]), .clk(clk_t), .Q(dataOut[11]), .reset(reset));  // open: Qn, preset
  D_Flip_Flop d_ff_16 (.D(dataIn[15]), .clk(clk_t), .Q(dataOut[15]), .reset(reset));  // open: Qn, preset

  // Other names for the same wires on the sheet: D0 = dataIn[0]; D1 = dataIn[1]; D2 = dataIn[2]; D3 = dataIn[3];
  //   D4 = dataIn[4]; D5 = dataIn[5]; D6 = dataIn[6]; D7 = dataIn[7]; D8 = dataIn[8]; D9 = dataIn[9];
  //   D10 = dataIn[10]; D11 = dataIn[11]; D12 = dataIn[12]; D13 = dataIn[13]; D14 = dataIn[14]; D15 = dataIn[15];
  //   Q0 = dataOut[0]; Q1 = dataOut[1]; Q2 = dataOut[2]; Q3 = dataOut[3]; Q4 = dataOut[4]; Q5 = dataOut[5];
  //   Q6 = dataOut[6]; Q7 = dataOut[7]; Q8 = dataOut[8]; Q9 = dataOut[9]; Q10 = dataOut[10]; Q11 = dataOut[11];
  //   Q12 = dataOut[12]; Q13 = dataOut[13]; Q14 = dataOut[14]; Q15 = dataOut[15]
endmodule

module programCounter (
  input  [15:0] in_1,
  input  in_2
);

  wire clock_1_out;

  Clock clock_1 (.out(clock_1_out));
  SingleRegister singleregister_1 (
    .dataIn(in_1), .reset(in_2), .clk(clock_1_out), .writeEnable(1'b1));  // open: dataOut
  Multiplexer #(.enable("false")) multiplexer_1 ();  // open: in0, in1, out, sel
  adder16Bit adder16bit_1 ();  // open: in_1, input2, input1, ovf, out1
endmodule

module adder16Bit (
  input  in_1,
  input  [15:0] input2,
  input  [15:0] input1,
  output ovf,
  output [15:0] out1
);

  wire adder1bit_1_cout, adder1bit_2_cout, adder1bit_3_cout, adder1bit_4_cout, adder1bit_5_cout,
       adder1bit_6_cout, adder1bit_7_cout, adder1bit_8_cout, adder1bit_9_cout, adder1bit_10_cout,
       adder1bit_11_cout, adder1bit_12_cout, adder1bit_13_cout, adder1bit_14_cout, adder1bit_15_cout,
       adder1bit_16_cout, xor_1_out, xor_2_out, xor_3_out, xor_4_out, xor_5_out, xor_6_out, xor_7_out,
       xor_8_out, xor_9_out, xor_10_out, xor_11_out, xor_12_out, xor_13_out, xor_14_out, xor_15_out,
       xor_16_out;

  xor xor_1 (xor_1_out, input2[0], in_1);
  adder1bit adder1bit_1 (.Cin(in_1), .A(input1[0]), .B(xor_1_out), .Sum(out1[0]), .Cout(adder1bit_1_cout));
  xor xor_2 (xor_2_out, input2[1], in_1);
  adder1bit adder1bit_2 (.Cin(adder1bit_1_cout), .A(input1[1]), .B(xor_2_out), .Sum(out1[1]), .Cout(adder1bit_2_cout));
  xor xor_3 (xor_3_out, input2[2], in_1);
  adder1bit adder1bit_3 (.Cin(adder1bit_2_cout), .A(input1[2]), .B(xor_3_out), .Sum(out1[2]), .Cout(adder1bit_3_cout));
  xor xor_4 (xor_4_out, input2[3], in_1);
  adder1bit adder1bit_4 (.Cin(adder1bit_3_cout), .A(input1[3]), .B(xor_4_out), .Sum(out1[3]), .Cout(adder1bit_4_cout));
  xor xor_5 (xor_5_out, input2[4], in_1);
  adder1bit adder1bit_5 (.Cin(adder1bit_4_cout), .A(input1[4]), .B(xor_5_out), .Sum(out1[4]), .Cout(adder1bit_5_cout));
  xor xor_6 (xor_6_out, input2[5], in_1);
  adder1bit adder1bit_6 (.Cin(adder1bit_5_cout), .A(input1[5]), .B(xor_6_out), .Sum(out1[5]), .Cout(adder1bit_6_cout));
  xor xor_7 (xor_7_out, input2[6], in_1);
  adder1bit adder1bit_7 (.Cin(adder1bit_6_cout), .A(input1[6]), .B(xor_7_out), .Sum(out1[6]), .Cout(adder1bit_7_cout));
  xor xor_8 (xor_8_out, input2[7], in_1);
  adder1bit adder1bit_8 (.Cin(adder1bit_7_cout), .A(input1[7]), .B(xor_8_out), .Sum(out1[7]), .Cout(adder1bit_8_cout));
  xor xor_9 (xor_9_out, input2[8], in_1);
  adder1bit adder1bit_9 (.Cin(adder1bit_8_cout), .A(input1[8]), .B(xor_9_out), .Sum(out1[8]), .Cout(adder1bit_9_cout));
  xor xor_10 (xor_10_out, input2[9], in_1);
  adder1bit adder1bit_10 (
    .Cin(adder1bit_9_cout), .A(input1[9]), .B(xor_10_out), .Sum(out1[9]), .Cout(adder1bit_10_cout));
  xor xor_11 (xor_11_out, input2[10], in_1);
  adder1bit adder1bit_11 (
    .Cin(adder1bit_10_cout), .A(input1[10]), .B(xor_11_out), .Sum(out1[10]), .Cout(adder1bit_11_cout));
  xor xor_12 (xor_12_out, input2[11], in_1);
  adder1bit adder1bit_12 (
    .Cin(adder1bit_11_cout), .A(input1[11]), .B(xor_12_out), .Sum(out1[11]), .Cout(adder1bit_12_cout));
  xor xor_13 (xor_13_out, input2[12], in_1);
  adder1bit adder1bit_13 (
    .Cin(adder1bit_12_cout), .A(input1[12]), .B(xor_13_out), .Sum(out1[12]), .Cout(adder1bit_13_cout));
  xor xor_14 (xor_14_out, input2[13], in_1);
  adder1bit adder1bit_14 (
    .Cin(adder1bit_13_cout), .A(input1[13]), .B(xor_14_out), .Sum(out1[13]), .Cout(adder1bit_14_cout));
  xor xor_15 (xor_15_out, input2[14], in_1);
  adder1bit adder1bit_15 (
    .Cin(adder1bit_14_cout), .A(input1[14]), .B(xor_15_out), .Sum(out1[14]), .Cout(adder1bit_15_cout));
  xor xor_16 (xor_16_out, input2[15], in_1);
  xor xor_17 (ovf, adder1bit_15_cout, adder1bit_16_cout);
  adder1bit adder1bit_16 (
    .Cin(adder1bit_15_cout), .A(input1[15]), .B(xor_16_out), .Sum(out1[15]), .Cout(adder1bit_16_cout));

  // Other names for the same wires on the sheet: a0 = input1[0]; a1 = input1[1]; a2 = input1[2]; a3 = input1[3];
  //   a4 = input1[4]; a5 = input1[5]; a6 = input1[6]; a7 = input1[7]; a8 = input1[8]; a9 = input1[9];
  //   a10 = input1[10]; a11 = input1[11]; a12 = input1[12]; a13 = input1[13]; a14 = input1[14]; a15 = input1[15];
  //   b0 = input2[0]; b1 = input2[1]; b2 = input2[2]; b3 = input2[3]; b4 = input2[4]; b5 = input2[5]; b6 = input2[6];
  //   b7 = input2[7]; b8 = input2[8]; b9 = input2[9]; b10 = input2[10]; b11 = input2[11]; b12 = input2[12];
  //   b13 = input2[13]; b14 = input2[14]; b15 = input2[15]; s0 = out1[0]; s1 = out1[1]; s2 = out1[2]; s3 = out1[3];
  //   s4 = out1[4]; s5 = out1[5]; s6 = out1[6]; s7 = out1[7]; s8 = out1[8]; s9 = out1[9]; s10 = out1[10];
  //   s11 = out1[11]; s12 = out1[12]; s13 = out1[13]; s14 = out1[14]; s15 = out1[15]; sub = in_1
endmodule

module adder1bit (
  input  Cin,
  input  A,
  input  B,
  output Sum,
  output Cout
);

  wire and_1_out, and_2_out, xor_1_out;

  and and_1 (and_1_out, B, A);
  xor xor_1 (xor_1_out, A, B);
  or or_1 (Cout, and_1_out, and_2_out);
  and and_2 (and_2_out, xor_1_out, Cin);
  xor xor_2 (Sum, Cin, xor_1_out);
endmodule

module decode (
  input  [15:0] input1,
  output [11:0] address,
  output [5:0] imm,
  output [2:0] Shamt,
  output [2:0] Rd,
  output [2:0] Rt,
  output [2:0] Rs,
  output [3:0] Opcode
);


  assign address = input1[11:0];
  assign imm = input1[5:0];
  assign Opcode = input1[15:12];
  assign Rd = input1[5:3];
  assign Rs = input1[11:9];
  assign Rt = input1[8:6];
  assign Shamt = input1[2:0];
endmodule

module rightShifter (
  input  [15:0] input1,
  input  [2:0] shamt,
  output [15:0] output1
);

  wire multiplexer_1_out, multiplexer_2_out, multiplexer_3_out, multiplexer_4_out, multiplexer_5_out,
       multiplexer_6_out, multiplexer_7_out, multiplexer_8_out, multiplexer_9_out, multiplexer_10_out,
       multiplexer_11_out, multiplexer_12_out, multiplexer_13_out, multiplexer_14_out, multiplexer_15_out,
       multiplexer_16_out, multiplexer_17_out, multiplexer_18_out, multiplexer_19_out, multiplexer_20_out,
       multiplexer_21_out, multiplexer_22_out, multiplexer_23_out, multiplexer_25_out, multiplexer_27_out,
       multiplexer_29_out, multiplexer_30_out, multiplexer_31_out, multiplexer_33_out, multiplexer_34_out,
       multiplexer_36_out, multiplexer_38_out;

  Multiplexer #(.enable("false")) multiplexer_1 (
    .in0(input1[0]), .in1(input1[1]), .out(multiplexer_1_out), .sel(shamt[0]));
  Multiplexer #(.enable("false")) multiplexer_2 (
    .in0(input1[1]), .in1(input1[2]), .out(multiplexer_2_out), .sel(shamt[0]));
  Multiplexer #(.enable("false")) multiplexer_3 (
    .in0(input1[2]), .in1(input1[3]), .out(multiplexer_3_out), .sel(shamt[0]));
  Multiplexer #(.enable("false")) multiplexer_4 (
    .in0(multiplexer_1_out), .in1(multiplexer_3_out), .out(multiplexer_4_out), .sel(shamt[1]));
  Multiplexer #(.enable("false")) multiplexer_5 (
    .in0(input1[2]), .in1(input1[4]), .out(multiplexer_5_out), .sel(shamt[0]));
  Multiplexer #(.enable("false")) multiplexer_6 (
    .in0(input1[2]), .in1(input1[5]), .out(multiplexer_6_out), .sel(shamt[0]));
  Multiplexer #(.enable("false")) multiplexer_7 (
    .in0(input1[5]), .in1(input1[6]), .out(multiplexer_7_out), .sel(shamt[0]));
  Multiplexer #(.enable("false")) multiplexer_8 (
    .in0(input1[6]), .in1(input1[7]), .out(multiplexer_8_out), .sel(shamt[0]));
  Multiplexer #(.enable("false")) multiplexer_9 (
    .in0(multiplexer_2_out), .in1(multiplexer_5_out), .out(multiplexer_9_out), .sel(shamt[1]));
  Multiplexer #(.enable("false")) multiplexer_10 (
    .in0(input1[7]), .in1(input1[8]), .out(multiplexer_10_out), .sel(shamt[0]));
  Multiplexer #(.enable("false")) multiplexer_11 (
    .in0(input1[8]), .in1(input1[9]), .out(multiplexer_11_out), .sel(shamt[0]));
  Multiplexer #(.enable("false")) multiplexer_12 (
    .in0(multiplexer_3_out), .in1(multiplexer_6_out), .out(multiplexer_12_out), .sel(shamt[1]));
  Multiplexer #(.enable("false")) multiplexer_13 (
    .in0(multiplexer_5_out), .in1(multiplexer_7_out), .out(multiplexer_13_out), .sel(shamt[1]));
  Multiplexer #(.enable("false")) multiplexer_14 (
    .in0(input1[9]), .in1(input1[10]), .out(multiplexer_14_out), .sel(shamt[0]));
  Multiplexer #(.enable("false")) multiplexer_15 (
    .in0(input1[10]), .in1(input1[11]), .out(multiplexer_15_out), .sel(shamt[0]));
  Multiplexer #(.enable("false")) multiplexer_16 (
    .in0(multiplexer_6_out), .in1(multiplexer_8_out), .out(multiplexer_16_out), .sel(shamt[1]));
  Multiplexer #(.enable("false")) multiplexer_17 (
    .in0(multiplexer_7_out), .in1(multiplexer_10_out), .out(multiplexer_17_out), .sel(shamt[1]));
  Multiplexer #(.enable("false")) multiplexer_18 (
    .in0(input1[11]), .in1(input1[12]), .out(multiplexer_18_out), .sel(shamt[0]));
  Multiplexer #(.enable("false")) multiplexer_19 (
    .in0(input1[12]), .in1(input1[13]), .out(multiplexer_19_out), .sel(shamt[0]));
  Multiplexer #(.enable("false")) multiplexer_20 (
    .in0(input1[13]), .in1(input1[14]), .out(multiplexer_20_out), .sel(shamt[0]));
  Multiplexer #(.enable("false")) multiplexer_21 (
    .in0(input1[14]), .in1(input1[15]), .out(multiplexer_21_out), .sel(shamt[0]));
  Multiplexer #(.enable("false")) multiplexer_22 (
    .in0(multiplexer_8_out), .in1(multiplexer_11_out), .out(multiplexer_22_out), .sel(shamt[1]));
  Multiplexer #(.enable("false")) multiplexer_23 (
    .in0(input1[15]), .in1(1'b0), .out(multiplexer_23_out), .sel(shamt[0]));
  Multiplexer #(.enable("false")) multiplexer_24 (
    .in0(multiplexer_4_out), .in1(multiplexer_16_out), .out(output1[0]), .sel(shamt[2]));
  Multiplexer #(.enable("false")) multiplexer_25 (
    .in0(multiplexer_10_out), .in1(multiplexer_14_out), .out(multiplexer_25_out), .sel(shamt[1]));
  Multiplexer #(.enable("false")) multiplexer_26 (
    .in0(multiplexer_9_out), .in1(multiplexer_17_out), .out(output1[1]), .sel(shamt[2]));
  Multiplexer #(.enable("false")) multiplexer_27 (
    .in0(multiplexer_11_out), .in1(multiplexer_15_out), .out(multiplexer_27_out), .sel(shamt[1]));
  Multiplexer #(.enable("false")) multiplexer_28 (
    .in0(multiplexer_12_out), .in1(multiplexer_22_out), .out(output1[2]), .sel(shamt[2]));
  Multiplexer #(.enable("false")) multiplexer_29 (
    .in0(multiplexer_14_out), .in1(multiplexer_18_out), .out(multiplexer_29_out), .sel(shamt[1]));
  Multiplexer #(.enable("false")) multiplexer_30 (
    .in0(multiplexer_15_out), .in1(multiplexer_19_out), .out(multiplexer_30_out), .sel(shamt[1]));
  Multiplexer #(.enable("false")) multiplexer_31 (
    .in0(multiplexer_18_out), .in1(multiplexer_20_out), .out(multiplexer_31_out), .sel(shamt[1]));
  Multiplexer #(.enable("false")) multiplexer_32 (
    .in0(multiplexer_13_out), .in1(multiplexer_25_out), .out(output1[3]), .sel(shamt[2]));
  Multiplexer #(.enable("false")) multiplexer_33 (
    .in0(multiplexer_19_out), .in1(multiplexer_21_out), .out(multiplexer_33_out), .sel(shamt[1]));
  Multiplexer #(.enable("false")) multiplexer_34 (
    .in0(multiplexer_20_out), .in1(multiplexer_23_out), .out(multiplexer_34_out), .sel(shamt[1]));
  Multiplexer #(.enable("false")) multiplexer_35 (
    .in0(multiplexer_16_out), .in1(multiplexer_27_out), .out(output1[4]), .sel(shamt[2]));
  Multiplexer #(.enable("false")) multiplexer_36 (
    .in0(multiplexer_21_out), .in1(1'b0), .out(multiplexer_36_out), .sel(shamt[1]));
  Multiplexer #(.enable("false")) multiplexer_37 (
    .in0(multiplexer_17_out), .in1(multiplexer_29_out), .out(output1[5]), .sel(shamt[2]));
  Multiplexer #(.enable("false")) multiplexer_38 (
    .in0(multiplexer_23_out), .in1(1'b0), .out(multiplexer_38_out), .sel(shamt[1]));
  Multiplexer #(.enable("false")) multiplexer_39 (
    .in0(multiplexer_22_out), .in1(multiplexer_30_out), .out(output1[6]), .sel(shamt[2]));
  Multiplexer #(.enable("false")) multiplexer_40 (
    .in0(multiplexer_25_out), .in1(multiplexer_31_out), .out(output1[7]), .sel(shamt[2]));
  Multiplexer #(.enable("false")) multiplexer_41 (
    .in0(multiplexer_27_out), .in1(multiplexer_33_out), .out(output1[8]), .sel(shamt[2]));
  Multiplexer #(.enable("false")) multiplexer_42 (
    .in0(multiplexer_29_out), .in1(multiplexer_34_out), .out(output1[9]), .sel(shamt[2]));
  Multiplexer #(.enable("false")) multiplexer_43 (
    .in0(multiplexer_30_out), .in1(multiplexer_36_out), .out(output1[10]), .sel(shamt[2]));
  Multiplexer #(.enable("false")) multiplexer_44 (
    .in0(multiplexer_31_out), .in1(multiplexer_38_out), .out(output1[11]), .sel(shamt[2]));
  Multiplexer #(.enable("false")) multiplexer_45 (
    .in0(multiplexer_33_out), .in1(1'b0), .out(output1[12]), .sel(shamt[2]));
  Multiplexer #(.enable("false")) multiplexer_46 (
    .in0(multiplexer_34_out), .in1(1'b0), .out(output1[13]), .sel(shamt[2]));
  Multiplexer #(.enable("false")) multiplexer_47 (
    .in0(multiplexer_36_out), .in1(1'b0), .out(output1[14]), .sel(shamt[2]));
  Multiplexer #(.enable("false")) multiplexer_48 (
    .in0(multiplexer_38_out), .in1(1'b0), .out(output1[15]), .sel(shamt[2]));

  // Other names for the same wires on the sheet: in0 = input1[0]; in1 = input1[1]; in2 = input1[2]; in3 = input1[3];
  //   in4 = input1[4]; in5 = input1[5]; in6 = input1[6]; in7 = input1[7]; in8 = input1[8]; in9 = input1[9];
  //   in10 = input1[10]; in11 = input1[11]; in12 = input1[12]; in13 = input1[13]; in14 = input1[14];
  //   in15 = input1[15]; out0 = output1[0]; out1 = output1[1]; out2 = output1[2]; out3 = output1[3];
  //   out4 = output1[4]; out5 = output1[5]; out6 = output1[6]; out7 = output1[7]; out8 = output1[8];
  //   out9 = output1[9]; out10 = output1[10]; out11 = output1[11]; out12 = output1[12]; out13 = output1[13];
  //   out14 = output1[14]; out15 = output1[15]; shift1 = shamt[0]; shift2 = shamt[1]; shift3 = shamt[2]
endmodule

module leftShifter (
  input  [15:0] input1,
  input  [2:0] shamt,
  output [15:0] output1
);

  wire multiplexer_1_out, multiplexer_2_out, multiplexer_3_out, multiplexer_4_out, multiplexer_5_out,
       multiplexer_6_out, multiplexer_7_out, multiplexer_8_out, multiplexer_9_out, multiplexer_10_out,
       multiplexer_11_out, multiplexer_12_out, multiplexer_13_out, multiplexer_14_out, multiplexer_15_out,
       multiplexer_16_out, multiplexer_17_out, multiplexer_18_out, multiplexer_19_out, multiplexer_20_out,
       multiplexer_21_out, multiplexer_22_out, multiplexer_23_out, multiplexer_25_out, multiplexer_27_out,
       multiplexer_29_out, multiplexer_30_out, multiplexer_31_out, multiplexer_33_out, multiplexer_34_out,
       multiplexer_36_out, multiplexer_38_out, out1;

  Multiplexer #(.enable("false")) multiplexer_1 (
    .in0(input1[15]), .in1(input1[14]), .out(multiplexer_1_out), .sel(shamt[0]));
  Multiplexer #(.enable("false")) multiplexer_2 (
    .in0(input1[14]), .in1(input1[13]), .out(multiplexer_2_out), .sel(shamt[0]));
  Multiplexer #(.enable("false")) multiplexer_3 (
    .in0(input1[13]), .in1(input1[12]), .out(multiplexer_3_out), .sel(shamt[0]));
  Multiplexer #(.enable("false")) multiplexer_4 (
    .in0(multiplexer_1_out), .in1(multiplexer_3_out), .out(multiplexer_4_out), .sel(shamt[1]));
  Multiplexer #(.enable("false")) multiplexer_5 (
    .in0(input1[13]), .in1(input1[11]), .out(multiplexer_5_out), .sel(shamt[0]));
  Multiplexer #(.enable("false")) multiplexer_6 (
    .in0(input1[13]), .in1(input1[10]), .out(multiplexer_6_out), .sel(shamt[0]));
  Multiplexer #(.enable("false")) multiplexer_7 (
    .in0(input1[10]), .in1(input1[9]), .out(multiplexer_7_out), .sel(shamt[0]));
  Multiplexer #(.enable("false")) multiplexer_8 (
    .in0(input1[9]), .in1(input1[8]), .out(multiplexer_8_out), .sel(shamt[0]));
  Multiplexer #(.enable("false")) multiplexer_9 (
    .in0(multiplexer_2_out), .in1(multiplexer_5_out), .out(multiplexer_9_out), .sel(shamt[1]));
  Multiplexer #(.enable("false")) multiplexer_10 (
    .in0(input1[8]), .in1(input1[7]), .out(multiplexer_10_out), .sel(shamt[0]));
  Multiplexer #(.enable("false")) multiplexer_11 (
    .in0(input1[7]), .in1(input1[6]), .out(multiplexer_11_out), .sel(shamt[0]));
  Multiplexer #(.enable("false")) multiplexer_12 (
    .in0(multiplexer_3_out), .in1(multiplexer_6_out), .out(multiplexer_12_out), .sel(shamt[1]));
  Multiplexer #(.enable("false")) multiplexer_13 (
    .in0(multiplexer_5_out), .in1(multiplexer_7_out), .out(multiplexer_13_out), .sel(shamt[1]));
  Multiplexer #(.enable("false")) multiplexer_14 (
    .in0(input1[6]), .in1(input1[5]), .out(multiplexer_14_out), .sel(shamt[0]));
  Multiplexer #(.enable("false")) multiplexer_15 (
    .in0(input1[5]), .in1(input1[4]), .out(multiplexer_15_out), .sel(shamt[0]));
  Multiplexer #(.enable("false")) multiplexer_16 (
    .in0(multiplexer_6_out), .in1(multiplexer_8_out), .out(multiplexer_16_out), .sel(shamt[1]));
  Multiplexer #(.enable("false")) multiplexer_17 (
    .in0(multiplexer_7_out), .in1(multiplexer_10_out), .out(multiplexer_17_out), .sel(shamt[1]));
  Multiplexer #(.enable("false")) multiplexer_18 (
    .in0(input1[4]), .in1(input1[3]), .out(multiplexer_18_out), .sel(shamt[0]));
  Multiplexer #(.enable("false")) multiplexer_19 (
    .in0(input1[3]), .in1(input1[2]), .out(multiplexer_19_out), .sel(shamt[0]));
  Multiplexer #(.enable("false")) multiplexer_20 (
    .in0(input1[2]), .in1(input1[1]), .out(multiplexer_20_out), .sel(shamt[0]));
  Multiplexer #(.enable("false")) multiplexer_21 (
    .in0(input1[1]), .in1(input1[0]), .out(multiplexer_21_out), .sel(shamt[0]));
  Multiplexer #(.enable("false")) multiplexer_22 (
    .in0(multiplexer_8_out), .in1(multiplexer_11_out), .out(multiplexer_22_out), .sel(shamt[1]));
  Multiplexer #(.enable("false")) multiplexer_23 (
    .in0(input1[0]), .in1(1'b0), .out(multiplexer_23_out), .sel(shamt[0]));
  Multiplexer #(.enable("false")) multiplexer_24 (
    .in0(multiplexer_4_out), .in1(multiplexer_16_out), .out(output1[15]), .sel(shamt[2]));
  Multiplexer #(.enable("false")) multiplexer_25 (
    .in0(multiplexer_10_out), .in1(multiplexer_14_out), .out(multiplexer_25_out), .sel(shamt[1]));
  Multiplexer #(.enable("false")) multiplexer_26 (
    .in0(multiplexer_9_out), .in1(multiplexer_17_out), .out(out1), .sel(shamt[2]));
  Multiplexer #(.enable("false")) multiplexer_27 (
    .in0(multiplexer_11_out), .in1(multiplexer_15_out), .out(multiplexer_27_out), .sel(shamt[1]));
  Multiplexer #(.enable("false")) multiplexer_28 (
    .in0(multiplexer_12_out), .in1(multiplexer_22_out), .out(output1[14]), .sel(shamt[2]));
  Multiplexer #(.enable("false")) multiplexer_29 (
    .in0(multiplexer_14_out), .in1(multiplexer_18_out), .out(multiplexer_29_out), .sel(shamt[1]));
  Multiplexer #(.enable("false")) multiplexer_30 (
    .in0(multiplexer_15_out), .in1(multiplexer_19_out), .out(multiplexer_30_out), .sel(shamt[1]));
  Multiplexer #(.enable("false")) multiplexer_31 (
    .in0(multiplexer_18_out), .in1(multiplexer_20_out), .out(multiplexer_31_out), .sel(shamt[1]));
  Multiplexer #(.enable("false")) multiplexer_32 (
    .in0(multiplexer_13_out), .in1(multiplexer_25_out), .out(output1[12]), .sel(shamt[2]));
  Multiplexer #(.enable("false")) multiplexer_33 (
    .in0(multiplexer_19_out), .in1(multiplexer_21_out), .out(multiplexer_33_out), .sel(shamt[1]));
  Multiplexer #(.enable("false")) multiplexer_34 (
    .in0(multiplexer_20_out), .in1(multiplexer_23_out), .out(multiplexer_34_out), .sel(shamt[1]));
  Multiplexer #(.enable("false")) multiplexer_35 (
    .in0(multiplexer_16_out), .in1(multiplexer_27_out), .out(output1[11]), .sel(shamt[2]));
  Multiplexer #(.enable("false")) multiplexer_36 (
    .in0(multiplexer_21_out), .in1(1'b0), .out(multiplexer_36_out), .sel(shamt[1]));
  Multiplexer #(.enable("false")) multiplexer_37 (
    .in0(multiplexer_17_out), .in1(multiplexer_29_out), .out(output1[10]), .sel(shamt[2]));
  Multiplexer #(.enable("false")) multiplexer_38 (
    .in0(multiplexer_23_out), .in1(1'b0), .out(multiplexer_38_out), .sel(shamt[1]));
  Multiplexer #(.enable("false")) multiplexer_39 (
    .in0(multiplexer_22_out), .in1(multiplexer_30_out), .out(output1[9]), .sel(shamt[2]));
  Multiplexer #(.enable("false")) multiplexer_40 (
    .in0(multiplexer_25_out), .in1(multiplexer_31_out), .out(output1[8]), .sel(shamt[2]));
  Multiplexer #(.enable("false")) multiplexer_41 (
    .in0(multiplexer_27_out), .in1(multiplexer_33_out), .out(output1[7]), .sel(shamt[2]));
  Multiplexer #(.enable("false")) multiplexer_42 (
    .in0(multiplexer_29_out), .in1(multiplexer_34_out), .out(output1[6]), .sel(shamt[2]));
  Multiplexer #(.enable("false")) multiplexer_43 (
    .in0(multiplexer_30_out), .in1(multiplexer_36_out), .out(output1[5]), .sel(shamt[2]));
  Multiplexer #(.enable("false")) multiplexer_44 (
    .in0(multiplexer_31_out), .in1(multiplexer_38_out), .out(output1[4]), .sel(shamt[2]));
  Multiplexer #(.enable("false")) multiplexer_45 (
    .in0(multiplexer_33_out), .in1(1'b0), .out(output1[3]), .sel(shamt[2]));
  Multiplexer #(.enable("false")) multiplexer_46 (
    .in0(multiplexer_34_out), .in1(1'b0), .out(output1[2]), .sel(shamt[2]));
  Multiplexer #(.enable("false")) multiplexer_47 (
    .in0(multiplexer_36_out), .in1(1'b0), .out(output1[1]), .sel(shamt[2]));
  Multiplexer #(.enable("false")) multiplexer_48 (
    .in0(multiplexer_38_out), .in1(1'b0), .out(output1[0]), .sel(shamt[2]));

  assign output1[13] = output1[14];

  // Other names for the same wires on the sheet: in15 = input1[0]; in14 = input1[1]; in13 = input1[2];
  //   in12 = input1[3]; in11 = input1[4]; in10 = input1[5]; in9 = input1[6]; in8 = input1[7]; in7 = input1[8];
  //   in6 = input1[9]; in5 = input1[10]; in4 = input1[11]; in3 = input1[12]; in2 = input1[13]; in1 = input1[14];
  //   in0 = input1[15]; out15 = output1[0]; out14 = output1[1]; out13 = output1[2]; out12 = output1[3];
  //   out11 = output1[4]; out10 = output1[5]; out9 = output1[6]; out8 = output1[7]; out7 = output1[8];
  //   out6 = output1[9]; out5 = output1[10]; out4 = output1[11]; out3 = output1[12]; out2 = output1[14];
  //   out0 = output1[15]; shift1 = shamt[0]; shift2 = shamt[1]; shift3 = shamt[2]
endmodule

module compare (
  input  [15:0] in_1,
  output equalToZero,
  output neg
);

  wire or_1_out;

  or or_1 (or_1_out, in_1[0], in_1[1], in_1[2], in_1[3], in_1[4], in_1[5], in_1[6], in_1[7], in_1[8], in_1[9], in_1[10], in_1[11], in_1[12], in_1[13], in_1[14], in_1[15]);
  not not_1 (equalToZero, or_1_out);

  assign neg = in_1[15];
endmodule

module control (
  input  [3:0] opcode,
  output in1,
  output ou1,
  output writeToMem,
  output Rwe,
  output Rdst,
  output ALUimm,
  output DMwe,
  output Rwd,
  output BR,
  output blt,
  output beqz,
  output jump0,
  output jump1
);

  wire and_1_out, and_2_out, and_3_out, and_4_out, demultiplexer_1_out0, demultiplexer_1_out1,
       demultiplexer_1_out2, demultiplexer_1_out3, demultiplexer_1_out4, demultiplexer_1_out5,
       demultiplexer_1_out6, demultiplexer_1_out11, demultiplexer_1_out12, demultiplexer_1_out13;

  Demultiplexer #(.select(4), .enable("false")) demultiplexer_1 (
    .out0(demultiplexer_1_out0), .out1(demultiplexer_1_out1), .out2(demultiplexer_1_out2),
    .out3(demultiplexer_1_out3), .out4(demultiplexer_1_out4), .out5(demultiplexer_1_out5),
    .out6(demultiplexer_1_out6), .out7(Rwd), .out8(DMwe), .out9(beqz), .out10(blt),
    .out11(demultiplexer_1_out11), .out12(demultiplexer_1_out12), .out13(demultiplexer_1_out13), .out14(in1),
    .out15(ou1), .in(1'b1), .sel(opcode));
  or or_1 (Rwe, demultiplexer_1_out0, demultiplexer_1_out1, demultiplexer_1_out2, demultiplexer_1_out3, demultiplexer_1_out4, demultiplexer_1_out5, demultiplexer_1_out6, Rwd, demultiplexer_1_out13, in1);
  or or_2 (Rdst, demultiplexer_1_out0, demultiplexer_1_out1, demultiplexer_1_out3, demultiplexer_1_out4, demultiplexer_1_out5, demultiplexer_1_out6, in1);
  or or_3 (ALUimm, demultiplexer_1_out2, Rwd, DMwe);
  or or_4 (BR, blt, beqz);
  and and_1 (and_1_out, demultiplexer_1_out11, ~demultiplexer_1_out12, ~demultiplexer_1_out13);  // AND_Gate
  or or_5 (jump0, and_1_out, and_2_out);
  and and_2 (and_2_out, ~demultiplexer_1_out11, ~demultiplexer_1_out12, demultiplexer_1_out13);  // AND_Gate
  and and_3 (and_3_out, ~demultiplexer_1_out11, demultiplexer_1_out12, ~demultiplexer_1_out13);  // AND_Gate
  or or_6 (jump1, and_3_out, and_4_out);
  and and_4 (and_4_out, ~demultiplexer_1_out11, ~demultiplexer_1_out12, demultiplexer_1_out13);  // AND_Gate

  assign writeToMem = Rwd;
endmodule
